# Fritzing sketch jardiniere connectee hydroponique (saved by Fritzing 0.9.3b)
circuit board: 8.46667cm x 5.64444cm
breadboards: 1

parts:
  Composant1 = Arduino Nano 33 IOT
  BAT1 = 12 battery [package=battery]
  R1 = Resistor [tolerance=±1% resistance=100k package=THT]
  R2 = Resistor [tolerance=±1% resistance=11k package=THT]
  U1 = LM2596-Step-Down-Converter [package=THT]
  RELAY1 = OMRON PCB Power Relay – G5LE [part_number="G5LE-1\n" package=THT]
  R4 = Resistor [tolerance=±1% resistance=8.2k package=THT]
  M1 = DC Motor
  Q1 = NPN-Transistor [part_number=S8050 package="TO92 [THT]"]
  D2 = Diode [package=diode-1n4148]
  R5 = PHOTOCELL [package=photocell]
  R6 = Resistor [tolerance=±1% resistance=5.1k package="2512 [SMD]"]

nets:
  N1: Composant1.RESET, Composant1.A7
  N2: Composant1.GND, Composant1.D13~, U1.pin3, RELAY1.COIL1, D2.C
  N3: Composant1.D4, R4.Pin_0
  N4: Composant1.D11/MOSI, Composant1.+5V
  N5: Composant1.VIN, BAT1.-, R2.Pin_1, U1.pin2, U1.pin4, R6.Pin_1
  N6: Composant1.A1, R5.P$2, R6.Pin_0
  N7: Composant1.A0, R1.Pin_1, R2.Pin_0
  N8: Composant1.3V3, R5.P$1
  N9: BAT1.+, R1.Pin_0, U1.pin1, RELAY1.B
  N10: RELAY1.A, M1.pin_1
  N11: RELAY1.C, M1.pin_2
  N12: RELAY1.COIL2, Q1.C, D2.A
  N13: R4.Pin_1, Q1.B

notes:
  Output 5.9V
  (<Vcoil max 6.5V)
  HK4100F-DC5V-SHG

custom parts:
  Arduino Nano 33 IOT: The Arduino Nano 33 IoT is the easiest and cheapest point of entry to enhance existing devices (and creating new ones) to be part of the IoT and designing pico-network applications. Whether you are looking at building a sensor network connected to your office or home router, or if you want to create a BLE device sending data to a cellphone, the Nano 33 IoT is your one-stop-solution for many of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
  12 battery: 12V lead acid type battery, like the Husqvarna YTH2448 12V 35AH battery. This is the mini version 1/4 the size of the actual battery to be closer to typical breadboard parts (around 2in wide rathher than 7in). The pads in pcb are sized to accomidate up to 14ga wire (as these batterys will deliver high currents.)
  LM2596-Step-Down-Converter: A dummy, proxy, ersatz, stand-in part for whatever you want. With 4 pins on a 100 mil inline pin header footprint.
